# Fritzing sketch led-button-distancesensor (saved by Fritzing 0.9.3b)
breadboards: 1

parts:
  Raspberry_Pi_1 = Raspberry Pi 3 [part_number=RPI-3-V1.2]
  hc-sr1 = hc-sr04
  R1 = Resistor [tolerance=±5% resistance=330 package=THT]
  R2 = Resistor [tolerance=±5% resistance=330 package=THT]
  R3 = Resistor [tolerance=±5% resistance=100 package=THT]
  LED2 = LED - 5mm [color="Red (633nm)" package="5 mm [THT]"]
  S2 = Pushbutton [package="[THT]"]
  R4 = Resistor [tolerance=±5% resistance=330 package="0402 [SMD]"]

nets:
  3V3: Raspberry_Pi_1.3v3, Raspberry_Pi_1.3V3, S2.Pin_3, S2.Pin_4
  GND: Raspberry_Pi_1.GND, hc-sr1.GND, R3.Pin_0, LED2.cathode
  N1: Raspberry_Pi_1.GIPO21, R4.Pin_0
  N2: Raspberry_Pi_1.GIPO16, S2.Pin_1, S2.Pin_2
  N3: Raspberry_Pi_1.GIPO24, R1.Pin_1, R2.Pin_1
  N4: Raspberry_Pi_1.GIPO18, hc-sr1.Trig
  5V: Raspberry_Pi_1.5V, hc-sr1.VCC
  N5: hc-sr1.Echo, R1.Pin_0
  N6: R2.Pin_0, R3.Pin_1
  N7: LED2.anode, R4.Pin_1
